# Fritzing sketch circuito v0.1 (saved by Fritzing 0.9.3b)

parts:
  U1 = NodeMCU V1.0
  GY1 = MPU-6050 Board GY-521 [form="♀ (female)" package=THT]
  DHT11_1 = DHT11 module
  M1 = BME280
  U2 = RF-LINK_RX [package=rf-link_rx]  # not connected
  J1 = female pin header, 4 pins [form="♀ (female)"]  # not connected
  sdCard1 = my_sdCard  # not connected
  Componente1 = Adafruit AMG8833 IR Camera FeatherWing [part_number=3622]  # not connected

nets:
  N1: U1.D1, GY1.pin3, M1.SCL
  N2: U1.D2, GY1.pin4, M1.SDA
  N3: GY1.pin2, DHT11_1.GND

notes:
  GY-NEO6MV2

custom parts:
  NodeMCU V1.0: ESP8266 based NodeMCU
  MPU-6050 Board GY-521: Acelerometro y Giroscopio MPU-6050 Board GY-521
  DHT11 module: https://cdn-learn.adafruit.com/downloads/pdf/dht.pdf DHT11 black pcb module reference by:https://github.com/adafruit/Fritzing-Library/blob/master/parts/DHT11%20Humitidy%20and%20Temperature%20Sensor.fzpz
  BME280: Temperature Humidity Barometric presure Sensor
  my_sdCard: micro sdCard Adapter with 90º pin header. Use a filtering Capacitor between CS and GND if needed. PCB View Pinouts are Reversed for laying parallel on PCB using a 90º pin header.
  Adafruit AMG8833 IR Camera FeatherWing: Thanks to the Panasonic AMG8833 8x8 GridEYE sensor, the Thermal Camera FeatherWing adds heat-vision to any Feather main board. Using our Feather Stacking Headers or Feather Female Headers you can connect a FeatherWing on top of your Feather board and let the board take flight! This sensor from Panasonic is an 8x8 array of IR thermal sensors. When connected to your Feather it will return an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
