# Fritzing sketch circuito v1 (saved by Fritzing 0.9.3b)

parts:
  U1 = NodeMCU V1.0
  GY1 = MPU-6050 Board GY-521 [form="♀ (female)" package=THT]
  DHT11_1 = DHT11 module
  M1 = BME280
  J1 = female pin header, 4 pins [form="♀ (female)"]
  sdCard1 = my_sdCard
  J2 = single row smd female pin header, 6 pins [form="♀ (female)"]
  J3 = single row smd female pin header, 7 pins [form="♀ (female)"]
  J4 = single row smd female pin header, 2 pins [form="♀ (female)"]
  J5 = single row smd female pin header, 2 pins [form="♀ (female)"]

nets:
  N1: U1.D1, GY1.pin3, M1.SCL, J2.pin3
  N2: U1.D2, GY1.pin4, M1.SDA, J2.pin4
  3V3: U1.3V3, GY1.pin1, DHT11_1.VCC, M1.VIN
  GND: U1.GND, M1.GND, J1.pin1, sdCard1.GND, J2.pin2, J3.pin1, J3.pin6, J3.pin7, J4.pin2, J5.pin2
  N3: U1.D5, sdCard1.SCK
  N4: U1.D6, sdCard1.MISO
  N5: U1.D7, sdCard1.MOSI
  N6: U1.D8, sdCard1.CS
  N7: U1.RX, J1.pin2, J3.pin4
  N8: U1.TX, J1.pin3, J3.pin5
  VIN: U1.Vin, sdCard1.VCC, J5.pin1
  N9: U1.A0, DHT11_1.DATA
  N10: GY1.pin2, DHT11_1.GND
  N11: J1.pin4, J2.pin1, J3.pin2, J4.pin1

notes:
  modulo gps(GY-NEO6MV2)
  Câmera Térmica Arduino AMG8833 8x8
  Módulo RF Wireless LoRa 433MHZ - E32 433T 30D (TTL-1W)
  fonte externa 3.3v
  fonte externa 5v
  Módulo Cartão Leitor Sd
  Sensor - Humidade e Temperatura
  Sensor - barômetro
  Sensor - giroscópio / Acelerômetro

custom parts:
  NodeMCU V1.0: ESP8266 based NodeMCU
  MPU-6050 Board GY-521: Acelerometro y Giroscopio MPU-6050 Board GY-521
  DHT11 module: https://cdn-learn.adafruit.com/downloads/pdf/dht.pdf DHT11 black pcb module reference by:https://github.com/adafruit/Fritzing-Library/blob/master/parts/DHT11%20Humitidy%20and%20Temperature%20Sensor.fzpz
  BME280: Temperature Humidity Barometric presure Sensor
  my_sdCard: micro sdCard Adapter with 90º pin header. Use a filtering Capacitor between CS and GND if needed. PCB View Pinouts are Reversed for laying parallel on PCB using a 90º pin header.
