# Fritzing sketch circuito v2.09 (saved by Fritzing 0.9.3b)

parts:
  J1 = female pin header, 4 pins [form="♀ (female)"]
  J2 = single row smd female pin header, 6 pins [form="♀ (female)"]
  J3 = single row smd female pin header, 7 pins [form="♀ (female)"]
  J4 = single row smd female pin header, 2 pins [form="♀ (female)"]
  J5 = single row smd female pin header, 2 pins [form="♀ (female)"]  # not connected

nets:
  N1: J1.pin4, J2.pin1, J3.pin2, J4.pin1

notes:
  modulo gps(GY-NEO6MV2)
  Câmera Térmica Arduino AMG8833 8x8
  Módulo RF Wireless LoRa 433MHZ - E32 433T 30D (TTL-1W)
  fonte externa 3.3v
  fonte externa 5v
  Módulo Cartão Leitor Sd
  Sensor - Humidade e Temperatura
  Sensor - barômetro
  Sensor - giroscópio / Acelerômetro
