# Fritzing sketch camada 1 satelite v2 (saved by Fritzing 0.9.3b)
circuit board: 4.60805cm x 6.39682cm
perfboards: 1

parts:
  sda-scl2 = male pin header, 2 pins [form="♂ (male)"]
  DHT11 = male pin header, 1 pin [form="♂ (male)"]
  J11 = female pin header, 4 pins [form="♀ (female)"]
  J14 = female pin header, 2 pins [form="♀ (female)"]
  sda-scl3 = male pin header, 2 pins [form="♂ (male)"]
  J15 = female pin header, 4 pins [form="♀ (female)"]  # not connected
  J16 = female pin header, 4 pins [form="♀ (female)"]  # not connected
  J10 = female pin header, 1 pin [form="♀ (female)"]
  J12 = male pin header, 3 pins [form="♂ (male)"]
  DHT12 = male pin header, 1 pin [form="♂ (male)"]
  DHT13 = male pin header, 1 pin [form="♂ (male)"]
  J9 = female pin header, 15 pins [form="♀ (female)"]
  J8 = female pin header, 15 pins [form="♀ (female)"]

nets:
  N1: sda-scl2.pin1, J8.pin2
  N2: sda-scl2.pin2, J8.pin3
  N3: DHT11.pin1, J8.pin4
  N4: J11.pin1, J8.pin11
  N5: J11.pin2, J8.pin10
  N6: J11.pin3, J8.pin9
  N7: J11.pin4, J8.pin8
  N8: J14.pin1, J8.pin13
  N9: J14.pin2, J8.pin12
  N10: sda-scl3.pin1, J12.pin3, DHT12.pin1, DHT13.pin1, J8.pin6
  N11: sda-scl3.pin2, J12.pin1, J8.pin7
  N12: J10.pin1, J9.pin15
  N13: J12.pin2, J8.pin5
