# Fritzing sketch camada 1-3 satelite v3 (saved by Fritzing 0.9.3b)
circuit board: 4.60805cm x 6.39682cm
circuit board: 4.61cm x 6.39682cm
circuit board: 4.60805cm x 6.39682cm
perfboards: 1

parts:
  Esp_Down = female pin header, 15 pins [form="♀ (female)"]
  Esp_Up = female pin header, 15 pins [form="♀ (female)"]
  BMP280 = female pin header, 4 pins [form="♀ (female)"]
  Mpu6050 = female pin header, 4 pins [form="♀ (female)"]
  R2 = Resistor [tolerance=±5% resistance=220 package=THT]
  R1 = Resistor [tolerance=±5% resistance=220 package=THT]
  R3 = Resistor [tolerance=±5% resistance=220 package=THT]
  D1 = Rectifier Diode [part_number=1N4001 package="300 mil [THT]"]
  l7805cv = PNP-Transistor [package="TO92 [THT]"]
  Servo = male pin header, 3 pins [form="♂ (male)"]  # not connected
  R6 = Resistor [tolerance=±5% resistance=220 package=THT]
  R4 = Resistor [tolerance=±5% resistance=220 package=THT]
  R5 = Resistor [tolerance=±5% resistance=220 package=THT]
  Esp_Down_B6 = female pin header, 2 pins [form="♀ (female)"]
  Esp_Up_B1 = female pin header, 6 pins [form="♀ (female)"]
  Esp_Up_B3 = female pin header, 8 pins [form="♀ (female)"]
  Energy = male pin header, 3 pins [form="♂ (male)"]
  Esp_Down_B4 = female pin header, 6 pins [form="♀ (female)"]
  Esp_Up_B7 = female pin header, 5 pins [form="♀ (female)"]
  Pin_B2 = male pin header, 6 pins [form="♂ (male)"]
  Pin_B3 = male pin header, 8 pins [form="♂ (male)"]
  Pin_B1 = male pin header, 6 pins [form="♂ (male)"]
  Pin_B4 = male pin header, 6 pins [form="♂ (male)"]
  Pin_B6 = male pin header, 2 pins [form="♂ (male)"]
  Pin_B5 = male pin header, 5 pins [form="♂ (male)"]
  sd_card = female pin header, 6 pins [form="♀ (female)"]
  Esp_Down_B2 = female pin header, 6 pins [form="♀ (female)"]
  Gps_Neo6mv2 = female pin header, 4 pins [form="♀ (female)"]
  Camera = female pin header, 4 pins [form="♀ (female)"]
  Lora_E220 = female pin header, 7 pins [form="♀ (female)"]

nets:
  N1: Esp_Down.pin1, Pin_B2.pin1
  N2: Esp_Down.pin4, Pin_B2.pin4
  N3: Esp_Down.pin10, Pin_B4.pin6
  N4: Esp_Down.pin11, Pin_B4.pin5
  N5: Esp_Down.pin14, Pin_B4.pin2
  N6: Esp_Down.pin15, Pin_B4.pin1
  N7: Esp_Up.pin1, Pin_B1.pin1
  N8: Esp_Up.pin2, BMP280.pin3, Mpu6050.pin2, Pin_B1.pin2
  N9: Esp_Up.pin3, BMP280.pin4, Mpu6050.pin1, Pin_B1.pin3
  N10: Esp_Up.pin4, Pin_B1.pin4
  N11: Esp_Up.pin5, Pin_B1.pin5
  N12: Esp_Up.pin8, Pin_B3.pin1
  N13: Esp_Up.pin9, Pin_B3.pin2
  N14: Esp_Up.pin10, Pin_B3.pin3
  N15: Esp_Up.pin11, Pin_B3.pin4
  N16: Esp_Up.pin14, BMP280.pin2, Mpu6050.pin3
  N17: Esp_Up.pin15, BMP280.pin1, Mpu6050.pin4
  N18: R2.Pin_0, R3.Pin_0, Esp_Down_B2.pin1
  N19: R2.Pin_1, R1.Pin_1
  N20: R1.Pin_0, D1.cathode, l7805cv.E
  N21: R3.Pin_1, l7805cv.B, Energy.pin1, Esp_Down_B4.pin2, sd_card.pin2
  N22: D1.anode, Energy.pin3
  N23: l7805cv.C, Esp_Down_B4.pin1, sd_card.pin1
  N24: R6.Pin_0, R4.Pin_0, R5.Pin_0, Esp_Down_B6.pin1, Gps_Neo6mv2.pin4, Camera.pin1, Lora_E220.pin1
  N25: R6.Pin_1, Lora_E220.pin5
  N26: R4.Pin_1, Esp_Up_B7.pin4, Lora_E220.pin3
  N27: R5.Pin_1, Esp_Up_B7.pin1, Gps_Neo6mv2.pin3, Lora_E220.pin4
  N28: Esp_Down_B6.pin2, Camera.pin4
  N29: Esp_Up_B1.pin1, Pin_B5.pin1
  N30: Esp_Up_B1.pin2, Pin_B5.pin2
  N31: Esp_Up_B1.pin3, Pin_B5.pin3
  N32: Esp_Up_B1.pin4, Pin_B5.pin4
  N33: Esp_Up_B1.pin5, Pin_B5.pin5
  N34: Esp_Up_B3.pin1, sd_card.pin5
  N35: Esp_Up_B3.pin2, sd_card.pin3
  N36: Esp_Up_B3.pin3, sd_card.pin4
  N37: Esp_Up_B3.pin4, sd_card.pin6
  N38: Esp_Down_B4.pin5, Pin_B6.pin1
  N39: Esp_Down_B4.pin6, Pin_B6.pin2
  N40: Esp_Up_B7.pin2, Camera.pin3
  N41: Esp_Up_B7.pin3, Camera.pin2
  N42: Esp_Up_B7.pin5, Gps_Neo6mv2.pin2
  N43: Gps_Neo6mv2.pin1, Lora_E220.pin2, Lora_E220.pin6, Lora_E220.pin7
