# Fritzing sketch camada 1 satelite (saved by Fritzing 0.9.3b)
circuit board: 4.60805cm x 6.39682cm
perfboards: 1

parts:
  J9 = female pin header, 15 pins [form="♀ (female)"]
  J8 = female pin header, 15 pins [form="♀ (female)"]
  R1 = Resistor [tolerance=±5% resistance=220 package=THT]
  R2 = Resistor [tolerance=±5% resistance=220 package=THT]
  D1 = Diode [package=diode-1n4148]
  R3 = Resistor [tolerance=±5% resistance=220 package=THT]
  sda-scl2 = male pin header, 2 pins [form="♂ (male)"]
  J12 = male pin header, 3 pins [form="♂ (male)"]
  J10 = female pin header, 2 pins [form="♀ (female)"]
  DHT11 = male pin header, 1 pin [form="♂ (male)"]
  J11 = female pin header, 4 pins [form="♀ (female)"]
  J14 = female pin header, 2 pins [form="♀ (female)"]
  sda-scl3 = male pin header, 2 pins [form="♂ (male)"]

nets:
  N1: J9.pin1, R1.Pin_0, R3.Pin_0
  N2: J9.pin14, R1.Pin_1, J10.pin1
  N3: J8.pin2, sda-scl2.pin1
  N4: J8.pin3, sda-scl2.pin2
  N5: J8.pin4, DHT11.pin1
  N6: J8.pin5, J12.pin2
  N7: J8.pin6, J12.pin1, sda-scl3.pin1
  N8: J8.pin7, J12.pin3, sda-scl3.pin2
  N9: J8.pin8, J11.pin4
  N10: J8.pin9, J11.pin3
  N11: J8.pin10, J11.pin2
  N12: J8.pin11, J11.pin1
  N13: J8.pin12, J14.pin2
  N14: J8.pin13, J14.pin1
  N15: R2.Pin_0, D1.C, R3.Pin_1
  N16: D1.A, J10.pin2
