# Fritzing sketch camada 2 satelite (saved by Fritzing 0.9.3b)
circuit board: 4.60805cm x 6.39682cm
perfboards: 1

parts:
  1-2 = female pin header, 1 pin [form="♀ (female)"]
  1-3 = female pin header, 1 pin [form="♀ (female)"]
  2 = female pin header, 4 pins [form="♀ (female)"]
  2_2 = female pin header, 4 pins [form="♀ (female)"]
  J17 = female pin header, 6 pins [form="♀ (female)"]
  2_3 = female pin header, 4 pins [form="♀ (female)"]
  3 = female pin header, 2 pins [form="♀ (female)"]
  sda-scl2 = male pin header, 2 pins [form="♂ (male)"]
  DHT11 = male pin header, 1 pin [form="♂ (male)"]
  J16 = female pin header, 4 pins [form="♀ (female)"]
  J15 = female pin header, 7 pins [form="♀ (female)"]
  2_4 = female pin header, 6 pins [form="♀ (female)"]
  5 = male pin header, 2 pins [form="♂ (male)"]
  1-4 = female pin header, 1 pin [form="♀ (female)"]
  1-5 = female pin header, 1 pin [form="♀ (female)"]
  1-6 = female pin header, 1 pin [form="♀ (female)"]
  1-7 = female pin header, 1 pin [form="♀ (female)"]
  D2 = Diode [package=diode-1n4148]
  J18 = female pin header, 2 pins [form="♀ (female)"]

nets:
  N1: 1-2.pin1, 1-3.pin1, J17.pin6, J16.pin1, J15.pin2, 2_4.pin2, 5.pin1, 1-6.pin1, 1-7.pin1, J18.pin1
  N2: 2.pin1, 2_2.pin1, J17.pin2, 2_3.pin1
  N3: 2.pin2, 2_2.pin2, J17.pin4, 2_3.pin2
  N4: 2.pin3, 2_2.pin3, J17.pin3, 2_3.pin3
  N5: 2.pin4, 2_2.pin4, J17.pin1, 2_3.pin4
  N6: J17.pin5, DHT11.pin1, J16.pin4, J15.pin1, J15.pin6, J15.pin7, 2_4.pin1, 5.pin2, 1-4.pin1, 1-5.pin1, D2.C
  N7: 3.pin1, J16.pin2, J15.pin5
  N8: sda-scl2.pin1, 2_4.pin3
  N9: sda-scl2.pin2, 2_4.pin4
  N10: D2.A, J18.pin2
