# Fritzing sketch design da placa da telemetria (saved by Fritzing 0.9.3b)
circuit board: 4.60805cm x 6.39682cm
perfboards: 1

parts:
  LED1 = LED - 3mm [color="Red (633nm)" package="3 mm [THT]"]
  J3 = female pin header, 2 pins [form="♀ (female)"]
  S1 = Momentary Switch [package=ksa_sealed_tac_switch]
  J4 = female pin header, 1 pin [form="♀ (female)"]
  J5 = female pin header, 1 pin [form="♀ (female)"]
  J6 = Generic female header - 4 pins [form="♀ (female)" package=THT]
  J7 = Generic female header - 4 pins [form="♀ (female)" package=THT]
  J9 = female pin header, 15 pins [form="♀ (female)"]
  J8 = female pin header, 15 pins [form="♀ (female)"]
  R2 = Resistor [tolerance=±5% resistance=220 package=THT]
  R3 = Resistor [tolerance=±5% resistance=220 package=THT]

nets:
  N1: LED1.cathode, R2.Pin_0
  N2: LED1.anode, J8.pin5
  N3: J3.pin1, J9.pin15
  N4: J3.pin2, J9.pin14
  VCC: S1.2, J6.vcc, J7.vcc, J8.pin15
  N5: S1.3, J8.pin4
  N6: S1.4, R3.Pin_1
  N7: J4.pin1, J8.pin7, R2.Pin_1
  N8: J5.pin1, J8.pin9
  GND: J6.gnd, J7.gnd, J8.pin14
  N9: J6.scl, J7.scl, J8.pin2
  N10: J6.sda, J7.sda, J8.pin3

custom parts:
  Generic female header - 4 pins: Generic female header
